# Fritzing sketch game (saved by Fritzing 0.9.3b)
breadboards: 1

parts:
  S1 = Pushbutton [package="[THT]"]
  S2 = Pushbutton [package="[THT]"]
  S3 = Pushbutton [package="[THT]"]
  R1 = Resistor [tolerance=±5% resistance=220 package=THT]
  LED2 = LED - 5mm [color="Red (633nm)" package="5 mm [THT]"]
  J1 = Piezo Speaker
  LED3 = smd LED [color="Green (555nm)" package="0603 [SMD]"]
  LED4 = smd LED [color="Yellow (595nm)" package="0603 [SMD]"]
  LED5 = LED - 5mm [color="Red (633nm)" package="5 mm [THT]"]
  LED6 = smd LED [color="Green (555nm)" package="0603 [SMD]"]
  R2 = Resistor [tolerance=±5% resistance=220 package=THT]
  R3 = Resistor [tolerance=±5% resistance=220 package=THT]
  R4 = Resistor [tolerance=±5% resistance=220 package=THT]
  R5 = Resistor [tolerance=±5% resistance=220 package=THT]
  R10 = Resistor [tolerance=±5% resistance=1k package=THT]
  R11 = Resistor [tolerance=±5% resistance=220 package=THT]
  Uno = Arduino Uno (Rev3)
  LED7 = LED - 5mm [color="Blue (430nm)" package="5 mm [THT]"]
  R12 = Resistor [tolerance=±5% resistance=220 package=THT]
  LED8 = RGB LED (com. cathode, rbg) [package="5 mm [THT]"]
  R14 = Resistor [tolerance=±5% resistance=220 package=THT]
  R13 = Resistor [tolerance=±5% resistance=220 package=THT]

nets:
  N1: S1.Pin_1, S1.Pin_2, S2.Pin_3, S2.Pin_4, S3.Pin_1, S3.Pin_2, R1.Pin_1, R2.Pin_1, R3.Pin_1, R4.Pin_1, R5.Pin_1, R10.Pin_0, Uno.GND, R12.Pin_1, LED8.common_cathode
  N2: S1.Pin_3, S1.Pin_4, Uno.D2
  N3: S2.Pin_1, S2.Pin_2, Uno.D3_PWM
  N4: S3.Pin_3, S3.Pin_4, Uno.D7
  N5: R1.Pin_0, LED3.cathode
  N6: LED2.cathode, R3.Pin_0
  N7: LED2.anode, Uno.D8
  N8: J1.pin1, R10.Pin_1
  N9: J1.pin2, Uno.D11_PWM/MOSI
  N10: LED3.anode, Uno.D10_PWM/SS
  N11: LED4.cathode, R2.Pin_0
  N12: LED4.anode, Uno.D9_PWM
  N13: LED5.cathode, R5.Pin_0
  N14: LED5.anode, Uno.D12/MISO
  N15: LED6.cathode, R4.Pin_0
  N16: LED6.anode, Uno.D13/SCK
  N17: R11.Pin_0, LED8.red_anode
  N18: R11.Pin_1, Uno.D6_PWM
  N19: Uno.A0, LED7.anode
  N20: Uno.D4, R14.Pin_1
  N21: Uno.D5_PWM, R13.Pin_1
  N22: LED7.cathode, R12.Pin_0
  N23: LED8.blue_anode, R13.Pin_0
  N24: LED8.green_anode, R14.Pin_0
